# Fritzing sketch fritzing sketch (saved by Fritzing 0.9.3b)
breadboards: 1

parts:
  Composant1 = Arduino Uno (Rev3)
  J2 = Basic Servo
  S1 = Toggle Switch [package=THT]
  LED1 = LED - 5mm [color="Red (633nm)" package="5 mm [THT]"]  # not connected
  Composant2 = Bluetooth HC-05 Macho
  J1 = Basic Servo
  R1 = Resistor [tolerance=±5% resistance=47k package=THT]
  VCC1 = Battery block 9V  # not connected

nets:
  N1: Composant1.D9_PWM, J2.pulse
  N2: Composant1.D10_PWM/SS, J1.pulse
  GND: Composant1.GND, J2.gnd, Composant2.GND, J1.gnd
  N3: Composant1.D0/RX, Composant2.TXD
  N4: Composant1.D1/TX, Composant2.RXD
  VCC: Composant1.5V, J2.vcc, Composant2.VCC, J1.vcc
  N5: Composant1.VIN, S1.COM, R1.Pin_0
